// Logisim project Logisim.circ as structural Verilog: 23 circuits, main circuit 12-bitRegister
module _12_bitRegister (
  input  [11:0] _12_Register,
  input  Clock,
  output [11:0] _12_RegisterOutput
);

  D_FlipFlop d_flipflop_1 (.D(_12_Register[0]), .Clock(Clock), .Q(_12_RegisterOutput[0]));  // open: out_4
  D_FlipFlop d_flipflop_2 (.D(_12_Register[1]), .Clock(Clock), .Q(_12_RegisterOutput[1]));  // open: out_4
  D_FlipFlop d_flipflop_3 (.D(_12_Register[2]), .Clock(Clock), .Q(_12_RegisterOutput[2]));  // open: out_4
  D_FlipFlop d_flipflop_4 (.D(_12_Register[3]), .Clock(Clock), .Q(_12_RegisterOutput[3]));  // open: out_4
  D_FlipFlop d_flipflop_5 (.D(_12_Register[4]), .Clock(Clock), .Q(_12_RegisterOutput[4]));  // open: out_4
  D_FlipFlop d_flipflop_6 (.D(_12_Register[5]), .Clock(Clock), .Q(_12_RegisterOutput[5]));  // open: out_4
  D_FlipFlop d_flipflop_7 (.D(_12_Register[6]), .Clock(Clock), .Q(_12_RegisterOutput[6]));  // open: out_4
  D_FlipFlop d_flipflop_8 (.D(_12_Register[7]), .Clock(Clock), .Q(_12_RegisterOutput[7]));  // open: out_4
  D_FlipFlop d_flipflop_9 (.D(_12_Register[8]), .Clock(Clock), .Q(_12_RegisterOutput[8]));  // open: out_4
  D_FlipFlop d_flipflop_10 (.D(_12_Register[9]), .Clock(Clock), .Q(_12_RegisterOutput[9]));  // open: out_4
  D_FlipFlop d_flipflop_11 (.D(_12_Register[10]), .Clock(Clock), .Q(_12_RegisterOutput[10]));  // open: out_4
  D_FlipFlop d_flipflop_12 (.D(_12_Register[11]), .Clock(Clock), .Q(_12_RegisterOutput[11]));  // open: out_4
endmodule

module IMM_Generatior (
  input  [6:0] in_1,
  output [19:0] out_2
);


  assign out_2 = {{14{in_1[6]}}, in_1[5:0]};
endmodule

module Register_File (
  input  enable,
  input  [3:0] WriteRegister,
  input  enableWrite,
  input  [3:0] ReadRegister1,
  input  Clock,
  input  [19:0] WriteData,
  input  [3:0] ReadRegister2,
  output [19:0] ReadData1,
  output [19:0] ReadData2
);

  wire and_1_out, and_2_out, and_3_out, and_4_out, and_5_out, and_6_out, and_7_out, and_8_out, and_9_out,
       and_10_out, and_11_out, and_12_out, and_13_out, and_14_out, and_15_out, and_16_out, and_17_out,
       and_18_out, and_19_out, and_20_out, and_21_out, and_22_out, and_23_out, and_24_out, and_25_out,
       and_26_out, and_27_out, and_28_out, and_29_out, and_30_out, and_31_out, and_32_out, decoder_1_out0,
       decoder_1_out1, decoder_1_out2, decoder_1_out3, decoder_1_out4, decoder_1_out5, decoder_1_out6,
       decoder_1_out7, decoder_1_out8, decoder_1_out9, decoder_1_out10, decoder_1_out11, decoder_1_out12,
       decoder_1_out13, decoder_1_out14, decoder_1_out15;
  wire [19:0] n20_bitregister_1_registeroutput, n20_bitregister_2_registeroutput,
       n20_bitregister_3_registeroutput, n20_bitregister_4_registeroutput, n20_bitregister_5_registeroutput,
       n20_bitregister_6_registeroutput, n20_bitregister_7_registeroutput, n20_bitregister_8_registeroutput,
       n20_bitregister_9_registeroutput, n20_bitregister_10_registeroutput,
       n20_bitregister_11_registeroutput, n20_bitregister_12_registeroutput,
       n20_bitregister_13_registeroutput, n20_bitregister_14_registeroutput,
       n20_bitregister_15_registeroutput, n20_bitregister_16_registeroutput;

  Decoder #(.select(4)) decoder_1 (
    .out0(decoder_1_out0), .out1(decoder_1_out1), .out2(decoder_1_out2), .out3(decoder_1_out3),
    .out4(decoder_1_out4), .out5(decoder_1_out5), .out6(decoder_1_out6), .out7(decoder_1_out7),
    .out8(decoder_1_out8), .out9(decoder_1_out9), .out10(decoder_1_out10), .out11(decoder_1_out11),
    .out12(decoder_1_out12), .out13(decoder_1_out13), .out14(decoder_1_out14), .out15(decoder_1_out15),
    .sel(WriteRegister));  // open: en
  and and_1 (and_1_out, decoder_1_out0, enableWrite);
  and and_2 (and_2_out, decoder_1_out1, enableWrite);
  and and_3 (and_3_out, decoder_1_out2, enableWrite);
  and and_4 (and_4_out, decoder_1_out3, enableWrite);
  and and_5 (and_5_out, decoder_1_out4, enableWrite);
  and and_6 (and_6_out, decoder_1_out5, enableWrite);
  and and_7 (and_7_out, decoder_1_out6, enableWrite);
  and and_8 (and_8_out, decoder_1_out7, enableWrite);
  and and_9 (and_9_out, decoder_1_out8, enableWrite);
  and and_10 (and_10_out, decoder_1_out9, enableWrite);
  and and_11 (and_11_out, decoder_1_out10, enableWrite);
  and and_12 (and_12_out, decoder_1_out11, enableWrite);
  and and_13 (and_13_out, decoder_1_out12, enableWrite);
  and and_14 (and_14_out, decoder_1_out13, enableWrite);
  and and_15 (and_15_out, decoder_1_out14, enableWrite);
  and and_16 (and_16_out, decoder_1_out15, enableWrite);
  and and_17 (and_17_out, and_1_out, Clock);
  and and_18 (and_18_out, and_2_out, Clock);
  and and_19 (and_19_out, and_3_out, Clock);
  and and_20 (and_20_out, and_4_out, Clock);
  and and_21 (and_21_out, and_5_out, Clock);
  and and_22 (and_22_out, and_6_out, Clock);
  and and_23 (and_23_out, and_7_out, Clock);
  and and_24 (and_24_out, and_8_out, Clock);
  and and_25 (and_25_out, and_9_out, Clock);
  and and_26 (and_26_out, and_10_out, Clock);
  and and_27 (and_27_out, and_11_out, Clock);
  and and_28 (and_28_out, and_12_out, Clock);
  and and_29 (and_29_out, and_13_out, Clock);
  and and_30 (and_30_out, and_14_out, Clock);
  and and_31 (and_31_out, and_15_out, Clock);
  and and_32 (and_32_out, and_16_out, Clock);
  _20_bitRegister u_20_bitregister_1 (
    .enable(enable), .Register(WriteData), .Clock(and_17_out),
    .RegisterOutput(n20_bitregister_1_registeroutput));
  _20_bitRegister u_20_bitregister_2 (
    .enable(enable), .Register(WriteData), .Clock(and_18_out),
    .RegisterOutput(n20_bitregister_2_registeroutput));
  _20_bitRegister u_20_bitregister_3 (
    .enable(enable), .Register(WriteData), .Clock(and_19_out),
    .RegisterOutput(n20_bitregister_3_registeroutput));
  _20_bitRegister u_20_bitregister_4 (
    .enable(enable), .Register(WriteData), .Clock(and_20_out),
    .RegisterOutput(n20_bitregister_4_registeroutput));
  _20_bitRegister u_20_bitregister_5 (
    .enable(enable), .Register(WriteData), .Clock(and_21_out),
    .RegisterOutput(n20_bitregister_5_registeroutput));
  _20_bitRegister u_20_bitregister_6 (
    .enable(enable), .Register(WriteData), .Clock(and_22_out),
    .RegisterOutput(n20_bitregister_6_registeroutput));
  _20_bitRegister u_20_bitregister_7 (
    .enable(enable), .Register(WriteData), .Clock(and_23_out),
    .RegisterOutput(n20_bitregister_7_registeroutput));
  _20_bitRegister u_20_bitregister_8 (
    .enable(enable), .Register(WriteData), .Clock(and_24_out),
    .RegisterOutput(n20_bitregister_8_registeroutput));
  _20_bitRegister u_20_bitregister_9 (
    .enable(enable), .Register(WriteData), .Clock(and_25_out),
    .RegisterOutput(n20_bitregister_9_registeroutput));
  _20_bitRegister u_20_bitregister_10 (
    .enable(enable), .Register(WriteData), .Clock(and_26_out),
    .RegisterOutput(n20_bitregister_10_registeroutput));
  _20_bitRegister u_20_bitregister_11 (
    .enable(enable), .Register(WriteData), .Clock(and_27_out),
    .RegisterOutput(n20_bitregister_11_registeroutput));
  _20_bitRegister u_20_bitregister_12 (
    .enable(enable), .Register(WriteData), .Clock(and_28_out),
    .RegisterOutput(n20_bitregister_12_registeroutput));
  _20_bitRegister u_20_bitregister_13 (
    .enable(enable), .Register(WriteData), .Clock(and_29_out),
    .RegisterOutput(n20_bitregister_13_registeroutput));
  _20_bitRegister u_20_bitregister_14 (
    .enable(enable), .Register(WriteData), .Clock(and_30_out),
    .RegisterOutput(n20_bitregister_14_registeroutput));
  _20_bitRegister u_20_bitregister_15 (
    .enable(enable), .Register(WriteData), .Clock(and_31_out),
    .RegisterOutput(n20_bitregister_15_registeroutput));
  _20_bitRegister u_20_bitregister_16 (
    .enable(enable), .Register(WriteData), .Clock(and_32_out),
    .RegisterOutput(n20_bitregister_16_registeroutput));
  Multiplexer #(.select(4), .width(20)) multiplexer_1 (
    .in0(n20_bitregister_1_registeroutput), .in1(n20_bitregister_2_registeroutput),
    .in2(n20_bitregister_3_registeroutput), .in3(n20_bitregister_4_registeroutput),
    .in4(n20_bitregister_5_registeroutput), .in5(n20_bitregister_6_registeroutput),
    .in6(n20_bitregister_7_registeroutput), .in7(n20_bitregister_8_registeroutput),
    .in8(n20_bitregister_9_registeroutput), .in9(n20_bitregister_10_registeroutput),
    .in10(n20_bitregister_11_registeroutput), .in11(n20_bitregister_12_registeroutput),
    .in12(n20_bitregister_13_registeroutput), .in13(n20_bitregister_14_registeroutput),
    .in14(n20_bitregister_15_registeroutput), .in15(n20_bitregister_16_registeroutput), .out(ReadData1),
    .sel(ReadRegister1));  // open: en
  Multiplexer #(.select(4), .width(20)) multiplexer_2 (
    .in0(n20_bitregister_1_registeroutput), .in1(n20_bitregister_2_registeroutput),
    .in2(n20_bitregister_3_registeroutput), .in3(n20_bitregister_4_registeroutput),
    .in4(n20_bitregister_5_registeroutput), .in5(n20_bitregister_6_registeroutput),
    .in6(n20_bitregister_7_registeroutput), .in7(n20_bitregister_8_registeroutput),
    .in8(n20_bitregister_9_registeroutput), .in9(n20_bitregister_10_registeroutput),
    .in10(n20_bitregister_11_registeroutput), .in11(n20_bitregister_12_registeroutput),
    .in12(n20_bitregister_13_registeroutput), .in13(n20_bitregister_14_registeroutput),
    .in14(n20_bitregister_15_registeroutput), .in15(n20_bitregister_16_registeroutput), .out(ReadData2),
    .sel(ReadRegister2));  // open: en
endmodule

module _20_bitRegister (
  input  Clock,
  input  enable,
  input  [19:0] Register,
  output [19:0] RegisterOutput
);

  wire and_1_out, and_2_out, and_3_out, and_4_out, and_5_out, and_6_out, and_7_out, and_8_out, and_9_out,
       and_10_out, and_11_out, and_12_out, and_13_out, and_14_out, and_15_out, and_16_out, and_17_out,
       and_18_out, and_19_out, and_20_out;

  and and_1 (and_1_out, enable, Clock);
  and and_2 (and_2_out, enable, Clock);
  and and_3 (and_3_out, enable, Clock);
  and and_4 (and_4_out, enable, Clock);
  and and_5 (and_5_out, enable, Clock);
  and and_6 (and_6_out, enable, Clock);
  and and_7 (and_7_out, enable, Clock);
  and and_8 (and_8_out, enable, Clock);
  and and_9 (and_9_out, enable, Clock);
  and and_10 (and_10_out, enable, Clock);
  and and_11 (and_11_out, enable, Clock);
  and and_12 (and_12_out, enable, Clock);
  and and_13 (and_13_out, enable, Clock);
  and and_14 (and_14_out, enable, Clock);
  and and_15 (and_15_out, enable, Clock);
  and and_16 (and_16_out, enable, Clock);
  and and_17 (and_17_out, enable, Clock);
  and and_18 (and_18_out, enable, Clock);
  and and_19 (and_19_out, enable, Clock);
  and and_20 (and_20_out, enable, Clock);
  D_FlipFlop d_flipflop_1 (.D(Register[0]), .Clock(and_1_out), .Q(RegisterOutput[0]));  // open: out_4
  D_FlipFlop d_flipflop_2 (.D(Register[1]), .Clock(and_2_out), .Q(RegisterOutput[1]));  // open: out_4
  D_FlipFlop d_flipflop_3 (.D(Register[2]), .Clock(and_3_out), .Q(RegisterOutput[2]));  // open: out_4
  D_FlipFlop d_flipflop_4 (.D(Register[3]), .Clock(and_4_out), .Q(RegisterOutput[3]));  // open: out_4
  D_FlipFlop d_flipflop_5 (.D(Register[4]), .Clock(and_5_out), .Q(RegisterOutput[4]));  // open: out_4
  D_FlipFlop d_flipflop_6 (.D(Register[5]), .Clock(and_6_out), .Q(RegisterOutput[5]));  // open: out_4
  D_FlipFlop d_flipflop_7 (.D(Register[6]), .Clock(and_7_out), .Q(RegisterOutput[6]));  // open: out_4
  D_FlipFlop d_flipflop_8 (.D(Register[7]), .Clock(and_8_out), .Q(RegisterOutput[7]));  // open: out_4
  D_FlipFlop d_flipflop_9 (.D(Register[8]), .Clock(and_9_out), .Q(RegisterOutput[8]));  // open: out_4
  D_FlipFlop d_flipflop_10 (.D(Register[9]), .Clock(and_10_out), .Q(RegisterOutput[9]));  // open: out_4
  D_FlipFlop d_flipflop_11 (.D(Register[10]), .Clock(and_11_out), .Q(RegisterOutput[10]));  // open: out_4
  D_FlipFlop d_flipflop_12 (.D(Register[11]), .Clock(and_12_out), .Q(RegisterOutput[11]));  // open: out_4
  D_FlipFlop d_flipflop_13 (.D(Register[12]), .Clock(and_13_out), .Q(RegisterOutput[12]));  // open: out_4
  D_FlipFlop d_flipflop_14 (.D(Register[13]), .Clock(and_14_out), .Q(RegisterOutput[13]));  // open: out_4
  D_FlipFlop d_flipflop_15 (.D(Register[14]), .Clock(and_15_out), .Q(RegisterOutput[14]));  // open: out_4
  D_FlipFlop d_flipflop_16 (.D(Register[15]), .Clock(and_16_out), .Q(RegisterOutput[15]));  // open: out_4
  D_FlipFlop d_flipflop_17 (.D(Register[16]), .Clock(and_17_out), .Q(RegisterOutput[16]));  // open: out_4
  D_FlipFlop d_flipflop_18 (.D(Register[17]), .Clock(and_18_out), .Q(RegisterOutput[17]));  // open: out_4
  D_FlipFlop d_flipflop_19 (.D(Register[18]), .Clock(and_19_out), .Q(RegisterOutput[18]));  // open: out_4
  D_FlipFlop d_flipflop_20 (.D(Register[19]), .Clock(and_20_out), .Q(RegisterOutput[19]));  // open: out_4
endmodule

module Full_Adder (
  input  Data1,
  input  Data2,
  input  Cin,
  output Sum,
  output Cout
);

  wire and_1_out, and_2_out, xor_1_out;

  xor xor_1 (xor_1_out, Data1, Data2);
  and and_1 (and_1_out, xor_1_out, Cin);
  and and_2 (and_2_out, Data1, Data2);
  xor xor_2 (Sum, xor_1_out, Cin);
  or or_1 (Cout, and_1_out, and_2_out);
endmodule

module D_FlipFlop (
  input  D,
  input  Clock,
  output Q,
  output out_4
);

  wire and_1_out, and_2_out, and_3_out, and_4_out, nor_1_out, nor_2_out, not_1_out, not_2_out, not_3_out;

  not not_1 (not_1_out, D);
  not not_2 (not_2_out, Clock);
  and and_1 (and_1_out, not_1_out, not_2_out);
  nor nor_1 (nor_1_out, and_1_out, nor_2_out);
  nor nor_2 (nor_2_out, nor_1_out, and_2_out);
  and and_2 (and_2_out, not_2_out, D);
  not not_3 (not_3_out, nor_1_out);
  and and_3 (and_3_out, not_3_out, Clock);
  and and_4 (and_4_out, Clock, nor_1_out);
  nor nor_3 (Q, and_3_out, out_4);
  nor nor_4 (out_4, Q, and_4_out);
endmodule

module ALU (
  input  [19:0] input1,
  input  [2:0] aluop,
  input  [19:0] input2,
  output [19:0] Output,
  output ZeroFlag,
  output NegativeFlag,
  output PF
);

  wire and_2_out, not_3_out, or_2_out;
  wire [19:0] and_1_out, n20_bit_adder_1_out_3, n20_bit_subtractor_1_out_3, not_1_out, or_1_out,
       shifter_1_out;

  _20_bit_adder u_20_bit_adder_1 (.src1(input1), .src2(input2), .out_3(n20_bit_adder_1_out_3));  // open: Cout
  _20_bit_Subtractor u_20_bit_subtractor_1 (
    .in_1(input1), .in_2(input2), .out_3(n20_bit_subtractor_1_out_3));  // open: out_4
  assign or_1_out = input1 | input2;  // OR_Gate or_1, 20 bits wide
  assign and_1_out = input1 & input2;  // AND_Gate and_1, 20 bits wide
  Shifter #(.width(20)) shifter_1 (.in(input2), .\dist (input1[4:0]), .out(shifter_1_out));
  assign not_1_out = ~and_1_out;  // NOT_Gate not_1, 20 bits wide
  Multiplexer #(.select(3), .width(20)) multiplexer_1 (
    .in0(n20_bit_adder_1_out_3), .in1(n20_bit_subtractor_1_out_3), .in2(or_1_out), .in3(not_1_out),
    .in4(shifter_1_out), .out({NegativeFlag, Output[18:0]}), .sel(aluop));  // open: in5, in6, in7, en
  or or_2 (or_2_out, Output[0], Output[9], Output[1], Output[2], Output[3], Output[4], Output[5], Output[6], Output[7], Output[8], Output[10], Output[11], Output[12], Output[13], Output[14], Output[15], Output[16], Output[17], Output[18], NegativeFlag);
  not not_2 (ZeroFlag, or_2_out);
  not not_3 (not_3_out, NegativeFlag);
  not not_4 (PF, and_2_out);
  and and_2 (and_2_out, ZeroFlag, not_3_out);

  assign Output[19] = NegativeFlag;
endmodule

module _20_bit_Subtractor (
  input  [19:0] in_1,
  input  [19:0] in_2,
  output [19:0] out_3,
  output out_4
);

  wire [19:0] binary_complementar_1_out_2;

  Binary_complementar binary_complementar_1 (.in_1(in_2), .out_2(binary_complementar_1_out_2));
  _20_bit_adder u_20_bit_adder_1 (.src1(in_1), .src2(binary_complementar_1_out_2), .out_3(out_3), .Cout(out_4));
endmodule

module _20_bit_adder (
  input  [19:0] src1,
  input  [19:0] src2,
  output [19:0] out_3,
  output Cout
);

  wire full_adder_1_cout, full_adder_2_cout, full_adder_3_cout, full_adder_4_cout, full_adder_5_cout,
       full_adder_6_cout, full_adder_7_cout, full_adder_8_cout, full_adder_9_cout, full_adder_10_cout,
       full_adder_11_cout, full_adder_12_cout, full_adder_13_cout, full_adder_14_cout, full_adder_15_cout,
       full_adder_16_cout, full_adder_17_cout, full_adder_18_cout, half_adder_1_cout;

  Half_Adder half_adder_1 (.input1(src2[0]), .input2(src1[0]), .Cout(half_adder_1_cout), .S(out_3[0]));
  Full_Adder full_adder_1 (
    .Data1(src1[1]), .Data2(src2[1]), .Cin(half_adder_1_cout), .Sum(out_3[1]), .Cout(full_adder_1_cout));
  Full_Adder full_adder_2 (
    .Data1(src1[2]), .Data2(src2[2]), .Cin(full_adder_1_cout), .Sum(out_3[2]), .Cout(full_adder_2_cout));
  Full_Adder full_adder_3 (
    .Data1(src1[3]), .Data2(src2[3]), .Cin(full_adder_2_cout), .Sum(out_3[3]), .Cout(full_adder_3_cout));
  Full_Adder full_adder_4 (
    .Data1(src1[4]), .Data2(src2[4]), .Cin(full_adder_3_cout), .Sum(out_3[4]), .Cout(full_adder_4_cout));
  Full_Adder full_adder_5 (
    .Data1(src1[5]), .Data2(src2[5]), .Cin(full_adder_4_cout), .Sum(out_3[5]), .Cout(full_adder_5_cout));
  Full_Adder full_adder_6 (
    .Data1(src1[6]), .Data2(src2[6]), .Cin(full_adder_5_cout), .Sum(out_3[6]), .Cout(full_adder_6_cout));
  Full_Adder full_adder_7 (
    .Data1(src1[7]), .Data2(src2[7]), .Cin(full_adder_6_cout), .Sum(out_3[7]), .Cout(full_adder_7_cout));
  Full_Adder full_adder_8 (
    .Data1(src1[8]), .Data2(src2[8]), .Cin(full_adder_7_cout), .Sum(out_3[8]), .Cout(full_adder_8_cout));
  Full_Adder full_adder_9 (
    .Data1(src1[9]), .Data2(src2[9]), .Cin(full_adder_8_cout), .Sum(out_3[9]), .Cout(full_adder_9_cout));
  Full_Adder full_adder_10 (
    .Data1(src1[10]), .Data2(src2[10]), .Cin(full_adder_9_cout), .Sum(out_3[10]), .Cout(full_adder_10_cout));
  Full_Adder full_adder_11 (
    .Data1(src1[11]), .Data2(src2[11]), .Cin(full_adder_10_cout), .Sum(out_3[11]), .Cout(full_adder_11_cout));
  Full_Adder full_adder_12 (
    .Data1(src1[12]), .Data2(src2[12]), .Cin(full_adder_11_cout), .Sum(out_3[12]), .Cout(full_adder_12_cout));
  Full_Adder full_adder_13 (
    .Data1(src1[13]), .Data2(src2[13]), .Cin(full_adder_12_cout), .Sum(out_3[13]), .Cout(full_adder_13_cout));
  Full_Adder full_adder_14 (
    .Data1(src1[14]), .Data2(src2[14]), .Cin(full_adder_13_cout), .Sum(out_3[14]), .Cout(full_adder_14_cout));
  Full_Adder full_adder_15 (
    .Data1(src1[15]), .Data2(src2[15]), .Cin(full_adder_14_cout), .Sum(out_3[15]), .Cout(full_adder_15_cout));
  Full_Adder full_adder_16 (
    .Data1(src1[16]), .Data2(src2[16]), .Cin(full_adder_15_cout), .Sum(out_3[16]), .Cout(full_adder_16_cout));
  Full_Adder full_adder_17 (
    .Data1(src1[17]), .Data2(src2[17]), .Cin(full_adder_16_cout), .Sum(out_3[17]), .Cout(full_adder_17_cout));
  Full_Adder full_adder_18 (
    .Data1(src1[18]), .Data2(src2[18]), .Cin(full_adder_17_cout), .Sum(out_3[18]), .Cout(full_adder_18_cout));
  Full_Adder full_adder_19 (.Data1(src1[19]), .Data2(src2[19]), .Cin(full_adder_18_cout), .Sum(out_3[19]), .Cout(Cout));
endmodule

module Binary_complementar (
  input  [19:0] in_1,
  output [19:0] out_2
);

  wire [19:0] not_1_out;

  assign not_1_out = ~in_1;  // NOT_Gate not_1, 20 bits wide
  _20_bit_adder u_20_bit_adder_1 (.src1(not_1_out), .src2(20'h1), .out_3(out_2));  // open: Cout
endmodule

module Instruction_Memory (
  input  [11:0] Address,
  input  ReadEnable,
  output [19:0] out_3
);

  ROM #(.addrWidth(12), .dataWidth(20)) rom_1 (.addr(Address), .data(out_3), .sel(ReadEnable));

  // Notes on the sheet:
  //   contents of rom_1 (hex, n*v repeats v):
  //   28005 28405 801 28436 7883f 68001 10c22 30c65 58c00 58820 51000 51420 60003 58c00 58820 29083 7149f
endmodule

module PC (
  input  next,
  input  enableJump,
  input  branch,
  input  clock,
  input  reset,
  input  [11:0] JumpAddress,
  input  [11:0] BranchAddress,
  output [11:0] nextPC
);

  wire and_1_out, not_1_out, or_1_out;
  wire [11:0] CurrentPC, multiplexer_1_out;

  not not_1 (not_1_out, next);
  or or_1 (or_1_out, enableJump, branch);
  and and_1 (and_1_out, not_1_out, or_1_out);
  Counter #(.width(12), .max('hfff)) counter_1 (
    .load(and_1_out), .D(CurrentPC), .count(next), .Q(nextPC), .clk(clock), .clr(reset));  // open: carry
  Multiplexer #(.width(12)) multiplexer_1 (
    .in0(JumpAddress), .in1(BranchAddress), .out(multiplexer_1_out), .sel(branch), .en(enableJump));
  _12bitAdder u_12bitadder_1 (.input1(nextPC), .input2(multiplexer_1_out), .sum(CurrentPC));
endmodule

module DataMemory (
  input  [11:0] Address,
  input  [19:0] DataInput,
  input  LoadEnable,
  input  WriteEnable,
  output [19:0] out_5
);

  wire clock_1_out;

  Clock clock_1 (.out(clock_1_out));
  RAM #(.addrWidth(12), .dataWidth(20), .bus("separate")) ram_1 (
    .addr(Address), .din(DataInput), .data(out_5), .str(WriteEnable), .clk(clock_1_out), .ld(LoadEnable));  // open: sel, clr
endmodule

module _12bitAdder (
  input  [11:0] input1,
  input  [11:0] input2,
  output [11:0] sum
);

  wire full_adder_2_cout, full_adder_3_cout, full_adder_4_cout, full_adder_5_cout, full_adder_6_cout,
       full_adder_7_cout, full_adder_8_cout, full_adder_9_cout, full_adder_10_cout, full_adder_11_cout,
       half_adder_1_cout;

  Full_Adder full_adder_1 (
    .Data1(input2[11]), .Data2(input1[11]), .Cin(full_adder_2_cout), .Sum(sum[11]));  // open: Cout
  Full_Adder full_adder_2 (
    .Data1(input2[10]), .Data2(input1[10]), .Cin(full_adder_4_cout), .Sum(sum[10]), .Cout(full_adder_2_cout));
  Full_Adder full_adder_3 (
    .Data1(input2[8]), .Data2(input1[8]), .Cin(full_adder_6_cout), .Sum(sum[8]), .Cout(full_adder_3_cout));
  Full_Adder full_adder_4 (
    .Data1(input2[9]), .Data2(input1[9]), .Cin(full_adder_3_cout), .Sum(sum[9]), .Cout(full_adder_4_cout));
  Full_Adder full_adder_5 (
    .Data1(input2[6]), .Data2(input1[6]), .Cin(full_adder_8_cout), .Sum(sum[6]), .Cout(full_adder_5_cout));
  Full_Adder full_adder_6 (
    .Data1(input2[7]), .Data2(input1[7]), .Cin(full_adder_5_cout), .Sum(sum[7]), .Cout(full_adder_6_cout));
  Full_Adder full_adder_7 (
    .Data1(input2[4]), .Data2(input1[4]), .Cin(full_adder_10_cout), .Sum(sum[4]), .Cout(full_adder_7_cout));
  Full_Adder full_adder_8 (
    .Data1(input2[5]), .Data2(input1[5]), .Cin(full_adder_7_cout), .Sum(sum[5]), .Cout(full_adder_8_cout));
  Full_Adder full_adder_9 (
    .Data1(input2[2]), .Data2(input1[2]), .Cin(full_adder_11_cout), .Sum(sum[2]), .Cout(full_adder_9_cout));
  Full_Adder full_adder_10 (
    .Data1(input2[3]), .Data2(input1[3]), .Cin(full_adder_9_cout), .Sum(sum[3]), .Cout(full_adder_10_cout));
  Half_Adder half_adder_1 (.input1(input1[0]), .input2(input2[0]), .Cout(half_adder_1_cout), .S(sum[0]));
  Full_Adder full_adder_11 (
    .Data1(input2[1]), .Data2(input1[1]), .Cin(half_adder_1_cout), .Sum(sum[1]), .Cout(full_adder_11_cout));
endmodule

module Half_Adder (
  input  input1,
  input  input2,
  output Cout,
  output S
);

  and and_1 (Cout, input1, input2);
  xor xor_1 (S, input1, input2);
endmodule

module Half_Comparison (
  input  a,
  input  b,
  output equal,
  output greater,
  output lower
);

  wire xor_1_out;

  xnor xnor_1 (equal, a, b);
  and and_1 (greater, a, xor_1_out);
  xor xor_1 (xor_1_out, a, b);
  and and_2 (lower, xor_1_out, b);
endmodule

module Full_Comparison (
  input  a,
  input  equal,
  input  greater,
  input  lower,
  input  b,
  output equal_2,
  output greater_2,
  output lower_2
);

  wire and_1_out, and_2_out, xnor_1_out;

  and and_1 (and_1_out, a, ~b, equal);  // AND_Gate
  and and_2 (and_2_out, ~a, b, equal);  // AND_Gate
  xnor xnor_1 (xnor_1_out, a, b);
  and and_3 (equal_2, xnor_1_out, equal);
  or or_1 (greater_2, and_1_out, greater);
  or or_2 (lower_2, and_2_out, lower);
endmodule

module Control_Unit (
  input  [19:0] register1,
  input  [19:0] register2,
  input  [19:0] _20_bit_input,
  output [3:0] DST_SRC_A1,
  output immsignal,
  output [3:0] SRC1_A2,
  output [19:0] aluinput1,
  output [3:0] SRC2,
  output [2:0] aluop,
  output [6:0] IMM7_ADDR7,
  output alucontrol,
  output [19:0] aluinput2,
  output redflag,
  output memRead,
  output memWrite,
  output jump,
  output [14:0] ADDR15,
  output [4:0] opcode,
  output branchsignal,
  output [10:0] ADDR11
);

  wire ADD, ADDI, BEQ, BGE, BGT, BLE, BLT, NAND, NANDI, OR, or_3_out, or_4_out, or_5_out, ORI, SLL, SLLI,
       SUB, SUBI;
  wire [6:0] IMM7_ADDR7_t;
  wire [19:0] imm_generatior_1_out_2, multiplexer_1_out;

  Decoder #(.select(5), .enable("false")) decoder_1 (
    .out0(ADD), .out1(SUB), .out2(OR), .out3(NAND), .out4(SLL), .out5(ADDI), .out6(ORI), .out7(NANDI),
    .out8(SUBI), .out9(SLLI), .out10(memRead), .out11(memWrite), .out12(jump), .out13(BEQ), .out14(BLT),
    .out15(BGT), .out16(BLE), .out17(BGE), .sel(_20_bit_input[19:15]));  // open: out18, out19, out20, out21, out22, out23, out24, out25, out26, out27, out28, out29, out30, out31
  or or_1 (immsignal, ADDI, ORI, NANDI, SUBI, SLLI);
  or or_2 (aluop[2], SLLI, SLL);
  or or_3 (or_3_out, NANDI, NAND);
  or or_4 (or_4_out, ORI, OR);
  or or_5 (or_5_out, SUBI, SUB);
  or or_6 (alucontrol, ADD, SUB, OR, NAND, SLL);
  BranchInstructions branchinstructions_1 (.PCOffset(IMM7_ADDR7_t));  // open: PC, a, b, nextPCBEQ, nextPCBLE, nextPCBGT, nextPCBGE, nextPCBLT
  or or_7 (redflag, alucontrol, memRead);
  or or_8 (aluop[0], or_3_out, or_5_out);
  or or_9 (aluop[1], or_4_out, or_5_out);
  or or_10 (branchsignal, BEQ, BLT, BGT, BLE, BGE);
  IMM_Generatior imm_generatior_1 (.in_1(_20_bit_input[6:0]), .out_2(imm_generatior_1_out_2));
  Multiplexer #(.width(20)) multiplexer_1 (
    .in0(register2), .in1(imm_generatior_1_out_2), .out(multiplexer_1_out), .sel(immsignal));  // open: en

  assign ADDR11 = _20_bit_input[10:0];
  assign ADDR15 = _20_bit_input[14:0];
  assign aluinput1 = register1;
  assign DST_SRC_A1 = _20_bit_input[14:11];
  assign IMM7_ADDR7 = _20_bit_input[6:0];
  assign opcode = _20_bit_input[19:15];
  assign SRC1_A2 = _20_bit_input[10:7];
  assign SRC2 = _20_bit_input[6:3];

  // Other names for the same wires on the sheet: ADDR7[6:0] = _20_bit_input[6:0]; IMM7[6:0] = _20_bit_input[6:0];
  //   A2[3:0] = _20_bit_input[10:7]; SRC1[3:0] = _20_bit_input[10:7]; A1[3:0] = _20_bit_input[14:11];
  //   DST[3:0] = _20_bit_input[14:11]; SRC[3:0] = _20_bit_input[14:11]; LD = memRead; ST = memWrite
endmodule

module BranchInstructions (
  input  [6:0] PCOffset,
  input  [11:0] PC,
  input  [19:0] a,
  input  [19:0] b,
  output [11:0] nextPCBEQ,
  output [11:0] nextPCBLE,
  output [11:0] nextPCBGT,
  output [11:0] nextPCBGE,
  output [11:0] nextPCBLT
);

  wire n20_bitcomparison_1_equal, n20_bitcomparison_1_greater, n20_bitcomparison_1_lower, or_1_out, or_2_out;
  wire [11:0] n12bitadder_2_sum, n12bitadder_3_sum, n12bitadder_4_sum, n12bitadder_5_sum, n12bitadder_6_sum,
       PCOffset_t, PCplusPCOffset;

  _12_bitIMM_Generator u_12_bitimm_generator_1 (.in_1(PCOffset), .out_2(PCOffset_t));
  _12bitAdder u_12bitadder_1 (.input1(PCOffset_t), .input2(PC), .sum(PCplusPCOffset));
  _20_bitComparison u_20_bitcomparison_1 (
    .a(a), .b(b), .equal(n20_bitcomparison_1_equal), .greater(n20_bitcomparison_1_greater),
    .lower(n20_bitcomparison_1_lower));
  _12bitAdder u_12bitadder_2 (.input1(PC), .input2(12'h1), .sum(n12bitadder_2_sum));
  _12bitAdder u_12bitadder_3 (.input1(PC), .input2(12'h1), .sum(n12bitadder_3_sum));
  Multiplexer #(.width(12)) multiplexer_1 (
    .in0(n12bitadder_2_sum), .in1(PCplusPCOffset), .out(nextPCBEQ), .sel(n20_bitcomparison_1_equal));  // open: en
  Multiplexer #(.width(12)) multiplexer_2 (
    .in0(n12bitadder_3_sum), .in1(PCplusPCOffset), .out(nextPCBGT), .sel(n20_bitcomparison_1_greater));  // open: en
  _12bitAdder u_12bitadder_4 (.input1(PC), .input2(12'h1), .sum(n12bitadder_4_sum));
  or or_1 (or_1_out, n20_bitcomparison_1_equal, n20_bitcomparison_1_greater);
  Multiplexer #(.width(12)) multiplexer_3 (
    .in0(n12bitadder_4_sum), .in1(PCplusPCOffset), .out(nextPCBLT), .sel(n20_bitcomparison_1_lower));  // open: en
  _12bitAdder u_12bitadder_5 (.input1(PC), .input2(12'h1), .sum(n12bitadder_5_sum));
  or or_2 (or_2_out, n20_bitcomparison_1_equal, n20_bitcomparison_1_lower);
  _12bitAdder u_12bitadder_6 (.input1(PC), .input2(12'h1), .sum(n12bitadder_6_sum));
  Multiplexer #(.width(12)) multiplexer_4 (
    .in0(n12bitadder_5_sum), .in1(PCplusPCOffset), .out(nextPCBLE), .sel(or_2_out));  // open: en
  Multiplexer #(.width(12)) multiplexer_5 (
    .in0(n12bitadder_6_sum), .in1(PCplusPCOffset), .out(nextPCBGE), .sel(or_1_out));  // open: en
endmodule

module _20_bitComparison (
  input  [19:0] a,
  input  [19:0] b,
  output equal,
  output greater,
  output lower
);

  wire full_comparison_1_equal_2, full_comparison_1_greater_2, full_comparison_1_lower_2,
       full_comparison_2_equal_2, full_comparison_2_greater_2, full_comparison_2_lower_2,
       full_comparison_3_equal_2, full_comparison_3_greater_2, full_comparison_3_lower_2,
       full_comparison_4_equal_2, full_comparison_4_greater_2, full_comparison_4_lower_2,
       full_comparison_5_equal_2, full_comparison_5_greater_2, full_comparison_5_lower_2,
       full_comparison_6_equal_2, full_comparison_6_greater_2, full_comparison_6_lower_2,
       full_comparison_7_equal_2, full_comparison_7_greater_2, full_comparison_7_lower_2,
       full_comparison_8_equal_2, full_comparison_8_greater_2, full_comparison_8_lower_2,
       full_comparison_9_equal_2, full_comparison_9_greater_2, full_comparison_9_lower_2,
       full_comparison_10_equal_2, full_comparison_10_greater_2, full_comparison_10_lower_2,
       full_comparison_11_equal_2, full_comparison_11_greater_2, full_comparison_11_lower_2,
       full_comparison_12_equal_2, full_comparison_12_greater_2, full_comparison_12_lower_2,
       full_comparison_13_equal_2, full_comparison_13_greater_2, full_comparison_13_lower_2,
       full_comparison_14_equal_2, full_comparison_14_greater_2, full_comparison_14_lower_2,
       full_comparison_15_equal_2, full_comparison_15_greater_2, full_comparison_15_lower_2,
       full_comparison_16_equal_2, full_comparison_16_greater_2, full_comparison_16_lower_2,
       full_comparison_17_equal_2, full_comparison_17_greater_2, full_comparison_17_lower_2,
       full_comparison_18_equal_2, full_comparison_18_greater_2, full_comparison_18_lower_2,
       half_comparison_1_equal, half_comparison_1_greater, half_comparison_1_lower;

  Full_Comparison full_comparison_1 (
    .a(a[18]), .equal(half_comparison_1_equal), .greater(half_comparison_1_greater),
    .lower(half_comparison_1_lower), .b(b[18]), .equal_2(full_comparison_1_equal_2),
    .greater_2(full_comparison_1_greater_2), .lower_2(full_comparison_1_lower_2));
  Half_Comparison half_comparison_1 (
    .a(a[19]), .b(b[19]), .equal(half_comparison_1_equal), .greater(half_comparison_1_greater),
    .lower(half_comparison_1_lower));
  Full_Comparison full_comparison_2 (
    .a(a[17]), .equal(full_comparison_1_equal_2), .greater(full_comparison_1_greater_2),
    .lower(full_comparison_1_lower_2), .b(b[17]), .equal_2(full_comparison_2_equal_2),
    .greater_2(full_comparison_2_greater_2), .lower_2(full_comparison_2_lower_2));
  Full_Comparison full_comparison_3 (
    .a(a[16]), .equal(full_comparison_2_equal_2), .greater(full_comparison_2_greater_2),
    .lower(full_comparison_2_lower_2), .b(b[16]), .equal_2(full_comparison_3_equal_2),
    .greater_2(full_comparison_3_greater_2), .lower_2(full_comparison_3_lower_2));
  Full_Comparison full_comparison_4 (
    .a(a[15]), .equal(full_comparison_3_equal_2), .greater(full_comparison_3_greater_2),
    .lower(full_comparison_3_lower_2), .b(b[15]), .equal_2(full_comparison_4_equal_2),
    .greater_2(full_comparison_4_greater_2), .lower_2(full_comparison_4_lower_2));
  Full_Comparison full_comparison_5 (
    .a(a[14]), .equal(full_comparison_4_equal_2), .greater(full_comparison_4_greater_2),
    .lower(full_comparison_4_lower_2), .b(b[14]), .equal_2(full_comparison_5_equal_2),
    .greater_2(full_comparison_5_greater_2), .lower_2(full_comparison_5_lower_2));
  Full_Comparison full_comparison_6 (
    .a(a[13]), .equal(full_comparison_5_equal_2), .greater(full_comparison_5_greater_2),
    .lower(full_comparison_5_lower_2), .b(b[13]), .equal_2(full_comparison_6_equal_2),
    .greater_2(full_comparison_6_greater_2), .lower_2(full_comparison_6_lower_2));
  Full_Comparison full_comparison_7 (
    .a(a[11]), .equal(full_comparison_8_equal_2), .greater(full_comparison_8_greater_2),
    .lower(full_comparison_8_lower_2), .b(b[11]), .equal_2(full_comparison_7_equal_2),
    .greater_2(full_comparison_7_greater_2), .lower_2(full_comparison_7_lower_2));
  Full_Comparison full_comparison_8 (
    .a(a[12]), .equal(full_comparison_6_equal_2), .greater(full_comparison_6_greater_2),
    .lower(full_comparison_6_lower_2), .b(b[12]), .equal_2(full_comparison_8_equal_2),
    .greater_2(full_comparison_8_greater_2), .lower_2(full_comparison_8_lower_2));
  Full_Comparison full_comparison_9 (
    .a(a[10]), .equal(full_comparison_7_equal_2), .greater(full_comparison_7_greater_2),
    .lower(full_comparison_7_lower_2), .b(b[10]), .equal_2(full_comparison_9_equal_2),
    .greater_2(full_comparison_9_greater_2), .lower_2(full_comparison_9_lower_2));
  Full_Comparison full_comparison_10 (
    .a(a[9]), .equal(full_comparison_9_equal_2), .greater(full_comparison_9_greater_2),
    .lower(full_comparison_9_lower_2), .b(b[9]), .equal_2(full_comparison_10_equal_2),
    .greater_2(full_comparison_10_greater_2), .lower_2(full_comparison_10_lower_2));
  Full_Comparison full_comparison_11 (
    .a(a[8]), .equal(full_comparison_10_equal_2), .greater(full_comparison_10_greater_2),
    .lower(full_comparison_10_lower_2), .b(b[8]), .equal_2(full_comparison_11_equal_2),
    .greater_2(full_comparison_11_greater_2), .lower_2(full_comparison_11_lower_2));
  Full_Comparison full_comparison_12 (
    .a(a[7]), .equal(full_comparison_11_equal_2), .greater(full_comparison_11_greater_2),
    .lower(full_comparison_11_lower_2), .b(b[7]), .equal_2(full_comparison_12_equal_2),
    .greater_2(full_comparison_12_greater_2), .lower_2(full_comparison_12_lower_2));
  Full_Comparison full_comparison_13 (
    .a(a[6]), .equal(full_comparison_12_equal_2), .greater(full_comparison_12_greater_2),
    .lower(full_comparison_12_lower_2), .b(b[6]), .equal_2(full_comparison_13_equal_2),
    .greater_2(full_comparison_13_greater_2), .lower_2(full_comparison_13_lower_2));
  Full_Comparison full_comparison_14 (
    .a(a[5]), .equal(full_comparison_13_equal_2), .greater(full_comparison_13_greater_2),
    .lower(full_comparison_13_lower_2), .b(b[5]), .equal_2(full_comparison_14_equal_2),
    .greater_2(full_comparison_14_greater_2), .lower_2(full_comparison_14_lower_2));
  Full_Comparison full_comparison_15 (
    .a(a[4]), .equal(full_comparison_14_equal_2), .greater(full_comparison_14_greater_2),
    .lower(full_comparison_14_lower_2), .b(b[4]), .equal_2(full_comparison_15_equal_2),
    .greater_2(full_comparison_15_greater_2), .lower_2(full_comparison_15_lower_2));
  Full_Comparison full_comparison_16 (
    .a(a[3]), .equal(full_comparison_15_equal_2), .greater(full_comparison_15_greater_2),
    .lower(full_comparison_15_lower_2), .b(b[3]), .equal_2(full_comparison_16_equal_2),
    .greater_2(full_comparison_16_greater_2), .lower_2(full_comparison_16_lower_2));
  Full_Comparison full_comparison_17 (
    .a(a[2]), .equal(full_comparison_16_equal_2), .greater(full_comparison_16_greater_2),
    .lower(full_comparison_16_lower_2), .b(b[2]), .equal_2(full_comparison_17_equal_2),
    .greater_2(full_comparison_17_greater_2), .lower_2(full_comparison_17_lower_2));
  Full_Comparison full_comparison_18 (
    .a(a[1]), .equal(full_comparison_17_equal_2), .greater(full_comparison_17_greater_2),
    .lower(full_comparison_17_lower_2), .b(b[1]), .equal_2(full_comparison_18_equal_2),
    .greater_2(full_comparison_18_greater_2), .lower_2(full_comparison_18_lower_2));
  Full_Comparison full_comparison_19 (
    .a(a[0]), .equal(full_comparison_18_equal_2), .greater(full_comparison_18_greater_2),
    .lower(full_comparison_18_lower_2), .b(b[0]), .equal_2(equal), .greater_2(greater), .lower_2(lower));
endmodule

module _12_bitIMM_Generator (
  input  [6:0] in_1,
  output [11:0] out_2
);


  assign out_2 = {{6{in_1[6]}}, in_1[5:0]};
endmodule

module main (
  output [19:0] out_1
);

  wire alu, alucontrol, branch, branchsignal, Clock, clock_t, comparison, dataMemRead, dataMemWrite,
       enableJump, enablePC, enableWrite, immsignal, jump, multiplexer_3_out, next, nextInst, or_1_out,
       redflag, regWrite, reset;
  wire [2:0] aluop;
  wire [3:0] DEST_SRC_OP1, DST_SRC_A1, multiplexer_1_out, SRC1, SRC1_OP2, SRC2;
  wire [4:0] opcode;
  wire [6:0] IMM7_ADDR7;
  wire [10:0] ADDR11;
  wire [11:0] BranchAddress, JumpAddress, pc_1_nextpc;
  wire [14:0] ADDR15;
  wire [19:0] aluinput1, aluinput2, dataMemResult, instruction_memory_1_out_3, multiplexer_2_out, REG1,
       REG1_data, REG2, REG2_data;

  Clock clock_1 (.out(clock_t));
  ALU alu_1 (
    .input1(aluinput1), .aluop(aluop), .input2(aluinput2), .Output(out_1));  // open: ZeroFlag, NegativeFlag, PF
  PC pc_1 (
    .next(next), .enableJump(enableJump), .branch(branch), .clock(clock_t), .reset(reset),
    .JumpAddress(JumpAddress), .BranchAddress(BranchAddress), .nextPC(pc_1_nextpc));
  FSM fsm_1 (
    .clock(Clock), .LD(dataMemRead), .ST(dataMemWrite), .jump(jump), .compraison(comparison), .alu(alu),
    .enableWrite(enableWrite), .enablePC(enablePC), .nextInst(nextInst), .enableJump(enableJump));
  Instruction_Memory instruction_memory_1 (
    .Address(pc_1_nextpc), .out_3(instruction_memory_1_out_3));  // open: ReadEnable
  Control_Unit control_unit_1 (
    .register1(REG1), .register2(REG2), ._20_bit_input(instruction_memory_1_out_3), .DST_SRC_A1(DST_SRC_A1),
    .immsignal(immsignal), .SRC1_A2(SRC1), .aluinput1(aluinput1), .SRC2(SRC2), .aluop(aluop),
    .IMM7_ADDR7(IMM7_ADDR7), .alucontrol(alucontrol), .aluinput2(aluinput2), .redflag(redflag),
    .memRead(dataMemRead), .memWrite(dataMemWrite), .ADDR15(ADDR15), .ADDR11(ADDR11), .opcode(opcode),
    .jump(jump), .branchsignal(branchsignal));
  Multiplexer #(.width(4), .enable("false")) multiplexer_1 (
    .in0(SRC2), .in1(DEST_SRC_OP1), .out(multiplexer_1_out), .sel(or_1_out));
  or or_1 (or_1_out, dataMemWrite, comparison);
  Multiplexer #(.width(20), .enable("false")) multiplexer_2 (
    .in0(dataMemResult), .in1(out_1), .out(multiplexer_2_out), .sel(dataMemRead));
  Register_File register_file_1 (
    .WriteRegister(DEST_SRC_OP1), .enableWrite(multiplexer_3_out), .ReadRegister1(SRC1_OP2), .Clock(Clock),
    .WriteData(multiplexer_2_out), .ReadRegister2(multiplexer_1_out), .ReadData1(REG1_data),
    .ReadData2(REG2_data));  // open: enable
  Multiplexer #(.enable("false")) multiplexer_3 (
    .in0(1'b0), .in1(regWrite), .out(multiplexer_3_out), .sel(enableWrite));
  RAM #(.addrWidth(12), .dataWidth(20), .bus("separate")) ram_1 (
    .addr({1'b0, ADDR11}), .din(aluinput2), .data(dataMemResult), .str(dataMemWrite), .sel(1'b1),
    .clk(Clock), .ld(dataMemRead));  // open: clr

  // Other names for the same wires on the sheet: ALUresult[19:0] = out_1
endmodule

module FSM (
  input  clock,
  input  LD,
  input  ST,
  input  jump,
  input  compraison,
  input  alu,
  output enableWrite,
  output enablePC,
  output nextInst,
  output enableJump
);

  wire alu_pc, alu_wr, branch_pc, controlled_buffer_1_out, controlled_buffer_2_out, controlled_buffer_3_out,
       controlled_buffer_4_out, controlled_buffer_5_out, counter_3_q, decoder_1_out0, decoder_1_out2,
       decoder_2_out0, decoder_2_out2, decoder_3_out0, decoder_3_out1, decoder_4_out1, decoder_4_out2,
       decoder_5_out1, decoder_5_out3, jump_pc, ld_pc, ld_wr, st_pc;
  wire [1:0] counter_1_q, counter_2_q, counter_4_q, counter_5_q;

  assign controlled_buffer_1_out = alu ? clock : 1'bz;  // Controlled_Buffer controlled_buffer_1
  assign controlled_buffer_2_out = LD ? clock : 1'bz;  // Controlled_Buffer controlled_buffer_2
  assign controlled_buffer_3_out = ST ? clock : 1'bz;  // Controlled_Buffer controlled_buffer_3
  Counter #(.width(2), .max('h2)) counter_1 (
    .Q(counter_1_q), .clk(controlled_buffer_1_out));  // open: load, D, count, carry, clr
  Counter #(.width(2), .max('h2)) counter_2 (
    .Q(counter_2_q), .clk(controlled_buffer_2_out));  // open: load, D, count, carry, clr
  Counter #(.width(1), .max('h1)) counter_3 (
    .Q(counter_3_q), .clk(controlled_buffer_3_out));  // open: load, D, count, carry, clr
  Counter #(.width(2), .max('h2)) counter_4 (
    .Q(counter_4_q), .clk(controlled_buffer_4_out));  // open: load, D, count, carry, clr
  assign controlled_buffer_4_out = compraison ? clock : 1'bz;  // Controlled_Buffer controlled_buffer_4
  assign controlled_buffer_5_out = jump ? clock : 1'bz;  // Controlled_Buffer controlled_buffer_5
  assign alu_pc = decoder_1_out0 ? 1'b0 : 1'bz;  // Controlled_Buffer controlled_buffer_6
  Decoder #(.select(2), .enable("false")) decoder_1 (
    .out0(decoder_1_out0), .out1(alu_wr), .out2(decoder_1_out2), .sel(counter_1_q));  // open: out3
  Decoder #(.select(2), .enable("false")) decoder_2 (
    .out0(decoder_2_out0), .out1(ld_wr), .out2(decoder_2_out2), .sel(counter_2_q));  // open: out3
  Decoder #(.enable("false")) decoder_3 (.out0(decoder_3_out0), .out1(decoder_3_out1), .sel(counter_3_q));
  Decoder #(.select(2), .enable("false")) decoder_4 (
    .out1(decoder_4_out1), .out2(decoder_4_out2), .sel(counter_4_q));  // open: out0, out3
  Counter #(.width(2), .max('h2)) counter_5 (
    .Q(counter_5_q), .clk(controlled_buffer_5_out));  // open: load, D, count, carry, clr
  assign alu_pc = decoder_1_out2 ? 1'b1 : 1'bz;  // Controlled_Buffer controlled_buffer_7
  assign ld_pc = decoder_2_out0 ? 1'b0 : 1'bz;  // Controlled_Buffer controlled_buffer_8
  assign ld_pc = decoder_2_out2 ? 1'b1 : 1'bz;  // Controlled_Buffer controlled_buffer_9
  assign st_pc = decoder_3_out0 ? 1'b0 : 1'bz;  // Controlled_Buffer controlled_buffer_10
  assign st_pc = decoder_3_out1 ? 1'b1 : 1'bz;  // Controlled_Buffer controlled_buffer_11
  assign branch_pc = decoder_4_out1 ? 1'b1 : 1'bz;  // Controlled_Buffer controlled_buffer_12
  assign branch_pc = decoder_4_out2 ? 1'b0 : 1'bz;  // Controlled_Buffer controlled_buffer_13
  assign jump_pc = decoder_5_out1 ? 1'b1 : 1'bz;  // Controlled_Buffer controlled_buffer_14
  Decoder #(.select(2), .enable("false")) decoder_5 (
    .out1(decoder_5_out1), .out3(decoder_5_out3), .sel(counter_5_q));  // open: out0, out2
  assign jump_pc = decoder_5_out3 ? 1'b0 : 1'bz;  // Controlled_Buffer controlled_buffer_15
  or or_1 (enableWrite, alu_wr, ld_wr);
  or or_2 (nextInst, alu_pc, ld_pc, st_pc);
  or or_3 (enableJump, branch_pc, branch_pc, jump_pc, jump_pc);
  or or_4 (enablePC, alu_pc, ld_pc, st_pc, branch_pc, jump_pc);

  // Other names for the same wires on the sheet: comparison = compraison

  // Notes on the sheet:
  //   ALU
  //   LD
  //   ST
  //   Branch
  //   Jump
endmodule
